// Logisim project 8bit_Computer_Farazz.circ as structural Verilog: 23 circuits, main circuit Main2
module Main2 (
  input  in_1,
  input  in_2,
  input  CounterEnable,
  input  in_4,
  input  in_5,
  input  in_6,
  input  [3:0] TestingData1,
  input  OutEnable1,
  input  Enable1,
  input  [7:0] TestData,
  input  OutEnableTest,
  input  OutEnablee,
  input  InternalEnable,
  input  Enabble,
  input  OutEnable2,
  input  Enable2,
  input  in_17,
  input  in_18,
  input  Enable,
  input  OutEnable,
  input  OutputEnable,
  input  Enablee,
  input  in_23,
  input  in_24,
  input  Enablle,
  output [3:0] out_26,
  output [3:0] out_27,
  output [7:0] out_28,
  output [7:0] out_29,
  output [7:0] RegisterA,
  output [7:0] ALURegister,
  output [7:0] out_32,
  output [7:0] RegisterB,
  output [2:0] out_34
);

  wire Clockk_out;
  wire [2:0] undriven;
  wire [3:0] bitselector_2_out, controlled_buffer_1_out, decimaldecoder_4_dout_2, decimaldecoder_4_dout_3,
       decimaldecoder_4_dout_4, decimaldecoder_4_dout_5, mar_1_dout;
  wire [7:0] alu_dewit_1_dout, bit_extender_1_out, InstructionRegister_dout, ram_1_dout;
  wire [15:0] decimaldecoder_1_dout, decimaldecoder_2_dout, decimaldecoder_3_dout, decimaldecoder_4_dout,
       decimaldecoder_5_dout;
  wire [31:16] decimaldecoder_1_dout_2, decimaldecoder_2_dout_2, decimaldecoder_3_dout_2,
       decimaldecoder_5_dout_2;

  DecimalDecoder decimaldecoder_1 (.Din(out_28), .Dout({decimaldecoder_1_dout_2, decimaldecoder_1_dout}));
  DecimalDecoder decimaldecoder_2 (.Din(RegisterA), .Dout({decimaldecoder_2_dout_2, decimaldecoder_2_dout}));
  DecimalDecoder decimaldecoder_3 (.Din(RegisterB), .Dout({decimaldecoder_3_dout_2, decimaldecoder_3_dout}));
  _7_Segment_Display u_7_segment_display_1 (
    .g(decimaldecoder_1_dout[15]), .f(decimaldecoder_1_dout[14]), .a(decimaldecoder_1_dout[13]),
    .b(decimaldecoder_1_dout[12]), .e(decimaldecoder_1_dout_2[31]), .d(decimaldecoder_1_dout_2[30]),
    .c(decimaldecoder_1_dout_2[29]), .dp(decimaldecoder_1_dout_2[28]));
  _7_Segment_Display u_7_segment_display_2 (
    .g(decimaldecoder_1_dout[11]), .f(decimaldecoder_1_dout[10]), .a(decimaldecoder_1_dout[9]),
    .b(decimaldecoder_1_dout[8]), .e(decimaldecoder_1_dout_2[27]), .d(decimaldecoder_1_dout_2[26]),
    .c(decimaldecoder_1_dout_2[25]), .dp(decimaldecoder_1_dout_2[24]));
  _7_Segment_Display u_7_segment_display_3 (
    .g(decimaldecoder_2_dout[15]), .f(decimaldecoder_2_dout[14]), .a(decimaldecoder_2_dout[13]),
    .b(decimaldecoder_2_dout[12]), .e(decimaldecoder_2_dout_2[31]), .d(decimaldecoder_2_dout_2[30]),
    .c(decimaldecoder_2_dout_2[29]), .dp(decimaldecoder_2_dout_2[28]));
  _7_Segment_Display u_7_segment_display_4 (
    .g(decimaldecoder_2_dout[11]), .f(decimaldecoder_2_dout[10]), .a(decimaldecoder_2_dout[9]),
    .b(decimaldecoder_2_dout[8]), .e(decimaldecoder_2_dout_2[27]), .d(decimaldecoder_2_dout_2[26]),
    .c(decimaldecoder_2_dout_2[25]), .dp(decimaldecoder_2_dout_2[24]));
  _7_Segment_Display u_7_segment_display_5 (
    .g(decimaldecoder_3_dout[15]), .f(decimaldecoder_3_dout[14]), .a(decimaldecoder_3_dout[13]),
    .b(decimaldecoder_3_dout[12]), .e(decimaldecoder_3_dout_2[31]), .d(decimaldecoder_3_dout_2[30]),
    .c(decimaldecoder_3_dout_2[29]), .dp(decimaldecoder_3_dout_2[28]));
  _7_Segment_Display u_7_segment_display_6 (
    .g(decimaldecoder_3_dout[11]), .f(decimaldecoder_3_dout[10]), .a(decimaldecoder_3_dout[9]),
    .b(decimaldecoder_3_dout[8]), .e(decimaldecoder_3_dout_2[27]), .d(decimaldecoder_3_dout_2[26]),
    .c(decimaldecoder_3_dout_2[25]), .dp(decimaldecoder_3_dout_2[24]));
  _7_Segment_Display u_7_segment_display_7 (
    .g(decimaldecoder_1_dout[7]), .f(decimaldecoder_1_dout[6]), .a(decimaldecoder_1_dout[5]),
    .b(decimaldecoder_1_dout[4]), .e(decimaldecoder_1_dout_2[23]), .d(decimaldecoder_1_dout_2[22]),
    .c(decimaldecoder_1_dout_2[21]), .dp(decimaldecoder_1_dout_2[20]));
  _7_Segment_Display u_7_segment_display_8 (
    .g(decimaldecoder_1_dout[3]), .f(decimaldecoder_1_dout[2]), .a(decimaldecoder_1_dout[1]),
    .b(decimaldecoder_1_dout[0]), .e(decimaldecoder_1_dout_2[19]), .d(decimaldecoder_1_dout_2[18]),
    .c(decimaldecoder_1_dout_2[17]), .dp(decimaldecoder_1_dout_2[16]));
  _7_Segment_Display u_7_segment_display_9 (
    .g(decimaldecoder_2_dout[7]), .f(decimaldecoder_2_dout[6]), .a(decimaldecoder_2_dout[5]),
    .b(decimaldecoder_2_dout[4]), .e(decimaldecoder_2_dout_2[23]), .d(decimaldecoder_2_dout_2[22]),
    .c(decimaldecoder_2_dout_2[21]), .dp(decimaldecoder_2_dout_2[20]));
  _7_Segment_Display u_7_segment_display_10 (
    .g(decimaldecoder_2_dout[3]), .f(decimaldecoder_2_dout[2]), .a(decimaldecoder_2_dout[1]),
    .b(decimaldecoder_2_dout[0]), .e(decimaldecoder_2_dout_2[19]), .d(decimaldecoder_2_dout_2[18]),
    .c(decimaldecoder_2_dout_2[17]), .dp(decimaldecoder_2_dout_2[16]));
  _7_Segment_Display u_7_segment_display_11 (
    .g(decimaldecoder_3_dout[7]), .f(decimaldecoder_3_dout[6]), .a(decimaldecoder_3_dout[5]),
    .b(decimaldecoder_3_dout[4]), .e(decimaldecoder_3_dout_2[23]), .d(decimaldecoder_3_dout_2[22]),
    .c(decimaldecoder_3_dout_2[21]), .dp(decimaldecoder_3_dout_2[20]));
  _7_Segment_Display u_7_segment_display_12 (
    .g(decimaldecoder_3_dout[3]), .f(decimaldecoder_3_dout[2]), .a(decimaldecoder_3_dout[1]),
    .b(decimaldecoder_3_dout[0]), .e(decimaldecoder_3_dout_2[19]), .d(decimaldecoder_3_dout_2[18]),
    .c(decimaldecoder_3_dout_2[17]), .dp(decimaldecoder_3_dout_2[16]));
  _7_Segment_Display u_7_segment_display_13 (
    .g(decimaldecoder_4_dout[3]), .f(decimaldecoder_4_dout[2]), .a(decimaldecoder_4_dout[1]),
    .b(decimaldecoder_4_dout[0]), .e(decimaldecoder_4_dout_2[3]), .d(decimaldecoder_4_dout_2[2]),
    .c(decimaldecoder_4_dout_2[1]), .dp(decimaldecoder_4_dout_2[0]));
  Clock Clockk (.out(Clockk_out));
  Counter #(.max('h3), .width(4)) ProgramCounter (
    .clr(in_2), .count(CounterEnable), .clk(Clockk_out), .D(controlled_buffer_1_out), .Q(out_26));  // open: load, up, carry
  DecimalDecoder decimaldecoder_4 (
    .Din(bit_extender_1_out),
    .Dout({decimaldecoder_4_dout_5, decimaldecoder_4_dout_4, decimaldecoder_4_dout_3, decimaldecoder_4_dout_2, decimaldecoder_4_dout}));
  assign bit_extender_1_out = {{4{out_26[3]}}, out_26};  // Bit_Extender bit_extender_1
  Register_Dewit InstructionRegister (
    .Output_Enable(OutEnablee), .Clock(Clockk_out), .Enable(Enabble), .Din(alu_dewit_1_dout),
    .Dout(InstructionRegister_dout), .Stored(out_28));  // open: Reset
  Register_Dewit RegA (
    .Output_Enable(in_17), .Reset(in_18), .Clock(Clockk_out), .Enable(Enable), .Din(alu_dewit_1_dout),
    .Stored(RegisterA));  // open: Dout
  ALU_Dewit alu_dewit_1 (
    .RegA(RegisterA), .RegB(RegisterB), .OutPut_Enable(OutputEnable), .Dout(alu_dewit_1_dout),
    .ALU_Register(ALURegister));  // open: Cout
  Register_Dewit RegB (
    .Output_Enable(in_23), .Reset(in_24), .Clock(Clockk_out), .Enable(Enablle), .Din(alu_dewit_1_dout),
    .Stored(RegisterB));  // open: Dout
  assign controlled_buffer_1_out = in_1 ? out_26 : 4'bz;  // Controlled_Buffer controlled_buffer_1
  BitSelector #(.group(4)) bitselector_1 (.in(InstructionRegister_dout), .out(controlled_buffer_1_out), .sel(1'b0));
  assign alu_dewit_1_dout = OutEnableTest ? TestData : 8'bz;  // Controlled_Buffer controlled_buffer_2
  LED D7 (.in(alu_dewit_1_dout[7]));
  LED D6 (.in(alu_dewit_1_dout[6]));
  LED D5 (.in(alu_dewit_1_dout[5]));
  LED D4 (.in(alu_dewit_1_dout[4]));
  LED D3 (.in(alu_dewit_1_dout[3]));
  LED D2 (.in(alu_dewit_1_dout[2]));
  LED D1 (.in(alu_dewit_1_dout[1]));
  LED D0 (.in(alu_dewit_1_dout[0]));
  assign alu_dewit_1_dout = InternalEnable ? out_29 : 8'bz;  // Controlled_Buffer controlled_buffer_3
  DecimalDecoder decimaldecoder_5 (.Din(out_32), .Dout({decimaldecoder_5_dout_2, decimaldecoder_5_dout}));
  MAR mar_1 (
    .Clock(Clockk_out), .Output_Enable(OutEnable1), .Enable(Enable1), .in_5(controlled_buffer_1_out),
    .Dout(mar_1_dout), .Stored(out_27));  // open: Reset
  Register_Dewit OutRegister (
    .Output_Enable(OutEnable), .Clock(Clockk_out), .Enable(Enablee), .Din(alu_dewit_1_dout),
    .Dout(alu_dewit_1_dout), .Stored(out_32));  // open: Reset
  _7_Segment_Display u_7_segment_display_14 (
    .g(decimaldecoder_5_dout[15]), .f(decimaldecoder_5_dout[14]), .a(decimaldecoder_5_dout[13]),
    .b(decimaldecoder_5_dout[12]), .e(decimaldecoder_5_dout_2[31]), .d(decimaldecoder_5_dout_2[30]),
    .c(decimaldecoder_5_dout_2[29]), .dp(decimaldecoder_5_dout_2[28]));
  _7_Segment_Display u_7_segment_display_15 (
    .g(decimaldecoder_5_dout[11]), .f(decimaldecoder_5_dout[10]), .a(decimaldecoder_5_dout[9]),
    .b(decimaldecoder_5_dout[8]), .e(decimaldecoder_5_dout_2[27]), .d(decimaldecoder_5_dout_2[26]),
    .c(decimaldecoder_5_dout_2[25]), .dp(decimaldecoder_5_dout_2[24]));
  Register_Dewit MBR (
    .Output_Enable(OutEnable2), .Clock(Clockk_out), .Enable(Enable2), .Din(alu_dewit_1_dout),
    .Dout(alu_dewit_1_dout), .Stored(out_29));  // open: Reset
  _7_Segment_Display u_7_segment_display_16 (
    .g(decimaldecoder_5_dout[7]), .f(decimaldecoder_5_dout[6]), .a(decimaldecoder_5_dout[5]),
    .b(decimaldecoder_5_dout[4]), .e(decimaldecoder_5_dout_2[23]), .d(decimaldecoder_5_dout_2[22]),
    .c(decimaldecoder_5_dout_2[21]), .dp(decimaldecoder_5_dout_2[20]));
  _7_Segment_Display u_7_segment_display_17 (
    .g(decimaldecoder_5_dout[3]), .f(decimaldecoder_5_dout[2]), .a(decimaldecoder_5_dout[1]),
    .b(decimaldecoder_5_dout[0]), .e(decimaldecoder_5_dout_2[19]), .d(decimaldecoder_5_dout_2[18]),
    .c(decimaldecoder_5_dout_2[17]), .dp(decimaldecoder_5_dout_2[16]));
  LED led_1 (.in(alu_dewit_1_dout[7]));
  assign mar_1_dout = in_4 ? TestingData1 : 4'bz;  // Controlled_Buffer controlled_buffer_4
  LED led_2 (.in(alu_dewit_1_dout[6]));
  LED led_3 (.in(alu_dewit_1_dout[5]));
  LED led_4 (.in(alu_dewit_1_dout[4]));
  LED led_5 (.in(alu_dewit_1_dout[3]));
  LED led_6 (.in(alu_dewit_1_dout[2]));
  LED led_7 (.in(alu_dewit_1_dout[1]));
  LED led_8 (.in(alu_dewit_1_dout[0]));
  RAM #(.addrWidth(4)) ram_1 (
    .addr(mar_1_dout), .we(in_6), .oe(in_5), .clk(Clockk_out), .din(alu_dewit_1_dout), .dout(ram_1_dout));
  assign alu_dewit_1_dout = in_5 ? ram_1_dout : 8'bz;  // Controlled_Buffer controlled_buffer_5
  Counter #(.max('h5), .width(3)) counter_1 (
    .clk(Clockk_out), .D(undriven), .Q(out_34));  // open: clr, load, up, count, carry
  // Probe on bitselector_2_out
  BitSelector #(.group(4)) bitselector_2 (.out(bitselector_2_out), .sel(1'b0));  // open: in

  // Notes on the sheet:
  //   Internal Address Bus(4Bits)
  //   Internal Buses
  //   External Address Bus
  //   External Data Bus
endmodule

module halfadder (
  input  A,
  input  B,
  output Sum,
  output Carry
);

  xor xor_1 (Sum, A, B);
  and and_1 (Carry, A, B);
endmodule

module FullAdder (
  input  Cin,
  input  A,
  input  B,
  output Sum,
  output Cout
);

  wire and_1_out, and_2_out, xor_1_out;

  xor xor_1 (xor_1_out, A, B);
  and and_1 (and_1_out, A, B);
  xor xor_2 (Sum, xor_1_out, Cin);
  and and_2 (and_2_out, xor_1_out, Cin);
  or or_1 (Cout, and_2_out, and_1_out);
endmodule

module Adder2bit (
  input  Cin,
  input  A1,
  input  B1,
  input  A2,
  input  B2,
  output Sum1,
  output Sum2,
  output Cout
);

  wire fulladder_1_cout;

  FullAdder fulladder_1 (.Cin(Cin), .A(A1), .B(B1), .Sum(Sum1), .Cout(fulladder_1_cout));
  FullAdder fulladder_2 (.Cin(fulladder_1_cout), .A(A2), .B(B2), .Sum(Sum2), .Cout(Cout));
endmodule

module Adder8bit (
  input  Cin,
  input  A1,
  input  B1,
  input  A2,
  input  B2,
  input  A3,
  input  B3,
  input  A4,
  input  B4,
  input  A5,
  input  B5,
  input  A6,
  input  B6,
  input  A7,
  input  B7,
  input  A8,
  input  B8,
  output Sum1,
  output Sum2,
  output Sum3,
  output Sum4,
  output Sum5,
  output Sum6,
  output Sum7,
  output Sum8,
  output Cout
);

  wire fulladder_1_cout, fulladder_2_cout, fulladder_3_cout, fulladder_4_cout, fulladder_5_cout,
       fulladder_6_cout, fulladder_7_cout;

  FullAdder fulladder_1 (.Cin(Cin), .A(A1), .B(B1), .Sum(Sum1), .Cout(fulladder_1_cout));
  FullAdder fulladder_2 (.Cin(fulladder_1_cout), .A(A2), .B(B2), .Sum(Sum2), .Cout(fulladder_2_cout));
  FullAdder fulladder_3 (.Cin(fulladder_2_cout), .A(A3), .B(B3), .Sum(Sum3), .Cout(fulladder_3_cout));
  FullAdder fulladder_4 (.Cin(fulladder_3_cout), .A(A4), .B(B4), .Sum(Sum4), .Cout(fulladder_4_cout));
  FullAdder fulladder_5 (.Cin(fulladder_4_cout), .A(A5), .B(B5), .Sum(Sum5), .Cout(fulladder_5_cout));
  FullAdder fulladder_6 (.Cin(fulladder_5_cout), .A(A6), .B(B6), .Sum(Sum6), .Cout(fulladder_6_cout));
  FullAdder fulladder_7 (.Cin(fulladder_6_cout), .A(A7), .B(B7), .Sum(Sum7), .Cout(fulladder_7_cout));
  FullAdder fulladder_8 (.Cin(fulladder_7_cout), .A(A8), .B(B8), .Sum(Sum8), .Cout(Cout));
endmodule

module latch (
  input  in_1,
  output out_2
);

  or or_1 (out_2, in_1, out_2);
endmodule

module S_R_Latch (
  output ouut,
  output inverted_out
);

  wire Reset_out, Set_out;

  Button Reset (.out(Reset_out));
  Button Set (.out(Set_out));
  nor nor_1 (ouut, Reset_out, inverted_out);
  nor nor_2 (inverted_out, ouut, Set_out);
endmodule

module D_Latch (
  input  Enable,
  input  D,
  output Outt
);

  wire and_1_out, and_2_out, nor_2_out, not_1_out;

  not not_1 (not_1_out, D);
  and and_1 (and_1_out, not_1_out, Enable);
  and and_2 (and_2_out, Enable, D);
  nor nor_1 (Outt, and_1_out, nor_2_out);
  nor nor_2 (nor_2_out, Outt, and_2_out);
endmodule

module Rising_Edge_edge_detector (
  output out_1
);

  wire clock_1_out, not_1_out, not_2_out, not_3_out;

  Clock clock_1 (.out(clock_1_out));
  not not_1 (not_1_out, clock_1_out);
  not not_2 (not_2_out, not_1_out);
  not not_3 (not_3_out, not_2_out);
  and and_1 (out_1, clock_1_out, not_3_out);
endmodule

module D_Flip_Flop (
  input  Enable,
  input  D,
  output Outt
);

  wire and_1_out, and_2_out, and_3_out, and_4_out, clock_1_out, nor_2_out, not_1_out, not_2_out, not_3_out,
       not_4_out;

  Clock clock_1 (.out(clock_1_out));
  not not_1 (not_1_out, clock_1_out);
  not not_2 (not_2_out, not_1_out);
  not not_3 (not_3_out, not_2_out);
  and and_1 (and_1_out, clock_1_out, not_3_out);
  and and_2 (and_2_out, and_1_out, Enable);
  not not_4 (not_4_out, D);
  and and_3 (and_3_out, not_4_out, and_2_out);
  and and_4 (and_4_out, and_2_out, D);
  nor nor_1 (Outt, and_3_out, nor_2_out);
  nor nor_2 (nor_2_out, Outt, and_4_out);
endmodule

module Adder8bit_subractor (
  input  Cin,
  input  A1,
  input  B1,
  input  A2,
  input  B2,
  input  A3,
  input  B3,
  input  A4,
  input  B4,
  input  A5,
  input  B5,
  input  A6,
  input  B6,
  input  A7,
  input  B7,
  input  A8,
  input  B8,
  output Sum1,
  output Sum2,
  output Sum3,
  output Sum4,
  output Sum5,
  output Sum6,
  output Sum7,
  output Sum8,
  output Cout
);

  wire fulladder_1_cout, fulladder_2_cout, fulladder_3_cout, fulladder_4_cout, fulladder_5_cout,
       fulladder_6_cout, fulladder_7_cout, not_1_out, not_2_out, not_3_out, not_4_out, not_5_out, not_6_out,
       not_7_out, not_8_out;

  not not_1 (not_1_out, B1);
  not not_2 (not_2_out, B2);
  not not_3 (not_3_out, B3);
  not not_4 (not_4_out, B4);
  not not_5 (not_5_out, B5);
  not not_6 (not_6_out, B6);
  not not_7 (not_7_out, B7);
  not not_8 (not_8_out, B8);
  FullAdder fulladder_1 (.Cin(Cin), .A(A1), .B(not_1_out), .Sum(Sum1), .Cout(fulladder_1_cout));
  FullAdder fulladder_2 (.Cin(fulladder_1_cout), .A(A2), .B(not_2_out), .Sum(Sum2), .Cout(fulladder_2_cout));
  FullAdder fulladder_3 (.Cin(fulladder_2_cout), .A(A3), .B(not_3_out), .Sum(Sum3), .Cout(fulladder_3_cout));
  FullAdder fulladder_4 (.Cin(fulladder_3_cout), .A(A4), .B(not_4_out), .Sum(Sum4), .Cout(fulladder_4_cout));
  FullAdder fulladder_5 (.Cin(fulladder_4_cout), .A(A5), .B(not_5_out), .Sum(Sum5), .Cout(fulladder_5_cout));
  FullAdder fulladder_6 (.Cin(fulladder_5_cout), .A(A6), .B(not_6_out), .Sum(Sum6), .Cout(fulladder_6_cout));
  FullAdder fulladder_7 (.Cin(fulladder_6_cout), .A(A7), .B(not_7_out), .Sum(Sum7), .Cout(fulladder_7_cout));
  FullAdder fulladder_8 (.Cin(fulladder_7_cout), .A(A8), .B(not_8_out), .Sum(Sum8), .Cout(Cout));
endmodule

module XOR_Toggle (
  input  Invert_Toggle,
  input  Data_Input,
  output out_3
);

  xor xor_1 (out_3, Invert_Toggle, Data_Input);
endmodule

module ADD_SUB_ADDER (
  input  ADDorSUBB,
  input  A1,
  input  B1,
  input  A2,
  input  B2,
  input  A3,
  input  B3,
  input  A4,
  input  B4,
  input  A5,
  input  B5,
  input  A6,
  input  B6,
  input  A7,
  input  B7,
  input  A8,
  input  B8,
  output out_18,
  output out_19,
  output out_20,
  output out_21,
  output out_22,
  output out_23,
  output out_24,
  output out_25,
  output Cout
);

  wire fulladder_1_cout, fulladder_2_cout, fulladder_3_cout, fulladder_4_cout, fulladder_5_cout,
       fulladder_6_cout, fulladder_7_cout, nor_1_out, nor_2_out, nor_3_out, nor_4_out, nor_5_out, nor_6_out,
       nor_7_out, nor_8_out;

  nor nor_1 (nor_1_out, ADDorSUBB, B1);
  nor nor_2 (nor_2_out, ADDorSUBB, B2);
  nor nor_3 (nor_3_out, ADDorSUBB, B3);
  nor nor_4 (nor_4_out, ADDorSUBB, B4);
  nor nor_5 (nor_5_out, ADDorSUBB, B5);
  nor nor_6 (nor_6_out, ADDorSUBB, B6);
  nor nor_7 (nor_7_out, ADDorSUBB, B7);
  nor nor_8 (nor_8_out, ADDorSUBB, B8);
  FullAdder fulladder_1 (.Cin(ADDorSUBB), .A(A1), .B(nor_1_out), .Sum(out_18), .Cout(fulladder_1_cout));
  FullAdder fulladder_2 (.Cin(fulladder_1_cout), .A(A2), .B(nor_2_out), .Sum(out_19), .Cout(fulladder_2_cout));
  FullAdder fulladder_3 (.Cin(fulladder_2_cout), .A(A3), .B(nor_3_out), .Sum(out_20), .Cout(fulladder_3_cout));
  FullAdder fulladder_4 (.Cin(fulladder_3_cout), .A(A4), .B(nor_4_out), .Sum(out_21), .Cout(fulladder_4_cout));
  FullAdder fulladder_5 (.Cin(fulladder_4_cout), .A(A5), .B(nor_5_out), .Sum(out_22), .Cout(fulladder_5_cout));
  FullAdder fulladder_6 (.Cin(fulladder_5_cout), .A(A6), .B(nor_6_out), .Sum(out_23), .Cout(fulladder_6_cout));
  FullAdder fulladder_7 (.Cin(fulladder_6_cout), .A(A7), .B(nor_7_out), .Sum(out_24), .Cout(fulladder_7_cout));
  FullAdder fulladder_8 (.Cin(fulladder_7_cout), .A(A8), .B(nor_8_out), .Sum(out_25), .Cout(Cout));
endmodule

module Multiplication4Bit (
  input  B4,
  input  B3,
  input  B2,
  input  B1,
  input  A4,
  input  A3,
  input  A2,
  input  A1,
  input  in_9,
  input  in_10,
  input  in_11,
  input  in_12,
  output P4,
  output P3,
  output P2,
  output P1,
  output out_17,
  output out_18,
  output out_19,
  output out_20
);

  wire adder4bit_2_cout, adder4bit_2_sum2, adder4bit_2_sum3, adder4bit_2_sum4, adder4bit_3_cout,
       adder4bit_3_sum2, adder4bit_3_sum3, adder4bit_3_sum4, and_1_out, and_2_out, and_3_out, and_4_out,
       and_5_out, and_6_out, and_7_out, and_8_out, and_9_out, and_10_out, and_11_out, and_12_out, and_13_out,
       and_14_out, and_15_out;

  and and_1 (and_1_out, A4, B4);
  and and_2 (and_2_out, A4, B4);
  and and_3 (and_3_out, A4, B4);
  and and_4 (and_4_out, A4, B4);
  and and_5 (and_5_out, A3, B3);
  and and_6 (and_6_out, A3, B3);
  and and_7 (and_7_out, A3, B3);
  and and_8 (and_8_out, A3, B3);
  Adder4bit adder4bit_1 (
    .Cin(in_12), .A1(and_4_out), .B1(adder4bit_2_sum2), .A2(and_3_out), .B2(adder4bit_2_sum3),
    .A3(and_2_out), .B3(adder4bit_2_sum4), .A4(and_1_out), .B4(adder4bit_2_cout), .Sum1(P4), .Sum2(out_20),
    .Sum3(out_19), .Sum4(out_18), .Cout(out_17));
  and and_9 (and_9_out, A1, B2);
  and and_10 (and_10_out, A1, B2);
  and and_11 (and_11_out, A1, B2);
  Adder4bit adder4bit_2 (
    .Cin(in_11), .A1(and_8_out), .B1(adder4bit_3_sum2), .A2(and_7_out), .B2(adder4bit_3_sum3),
    .A3(and_6_out), .B3(adder4bit_3_sum4), .A4(and_5_out), .B4(adder4bit_3_cout), .Sum1(P3),
    .Sum2(adder4bit_2_sum2), .Sum3(adder4bit_2_sum3), .Sum4(adder4bit_2_sum4), .Cout(adder4bit_2_cout));
  and and_12 (and_12_out, A1, B2);
  and and_13 (and_13_out, A1, B1);
  and and_14 (and_14_out, A1, B1);
  and and_15 (and_15_out, A1, B1);
  and and_16 (P1, A1, B1);
  Adder4bit adder4bit_3 (
    .Cin(in_9), .A1(and_12_out), .B1(and_15_out), .A2(and_11_out), .B2(and_14_out), .A3(and_10_out),
    .B3(and_13_out), .A4(and_9_out), .B4(in_10), .Sum1(P2), .Sum2(adder4bit_3_sum2), .Sum3(adder4bit_3_sum3),
    .Sum4(adder4bit_3_sum4), .Cout(adder4bit_3_cout));

  assign A2 = A1;
endmodule

module Adder4bit (
  input  Cin,
  input  A1,
  input  B1,
  input  A2,
  input  B2,
  input  A3,
  input  B3,
  input  A4,
  input  B4,
  output Sum1,
  output Sum2,
  output Sum3,
  output Sum4,
  output Cout
);

  wire fulladder_1_cout, fulladder_2_cout, fulladder_3_cout;

  FullAdder fulladder_1 (.Cin(Cin), .A(A1), .B(B1), .Sum(Sum1), .Cout(fulladder_1_cout));
  FullAdder fulladder_2 (.Cin(fulladder_1_cout), .A(A2), .B(B2), .Sum(Sum2), .Cout(fulladder_2_cout));
  FullAdder fulladder_3 (.Cin(fulladder_2_cout), .A(A3), .B(B3), .Sum(Sum3), .Cout(fulladder_3_cout));
  FullAdder fulladder_4 (.Cin(fulladder_3_cout), .A(A4), .B(B4), .Sum(Sum4), .Cout(Cout));
endmodule

module Register8bit (
  input  Enable,
  input  D,
  output out_3,
  output out_4,
  output out_5,
  output out_6,
  output out_7,
  output out_8,
  output out_9,
  output out_10
);

  wire and_1_out, and_2_out, and_3_out, and_4_out, and_5_out, and_6_out, and_7_out, and_8_out, and_9_out,
       and_10_out, and_11_out, and_12_out, and_13_out, and_14_out, and_15_out, and_16_out, and_17_out,
       and_18_out, and_19_out, and_20_out, and_21_out, and_22_out, and_23_out, and_24_out, and_25_out,
       and_26_out, and_27_out, and_28_out, and_29_out, and_30_out, and_31_out, and_32_out, clock_1_out,
       nor_2_out, nor_4_out, nor_6_out, nor_8_out, nor_10_out, nor_12_out, nor_14_out, nor_16_out, not_1_out,
       not_2_out, not_3_out, not_4_out, not_5_out, not_6_out, not_7_out, not_8_out, not_9_out, not_10_out,
       not_11_out, not_12_out, not_13_out, not_14_out, not_15_out, not_16_out, not_17_out, not_18_out,
       not_19_out, not_20_out, not_21_out, not_22_out, not_23_out, not_24_out, not_25_out, not_26_out,
       not_27_out, not_28_out, not_29_out, not_30_out, not_31_out, not_32_out;

  Clock clock_1 (.out(clock_1_out));
  not not_1 (not_1_out, clock_1_out);
  not not_2 (not_2_out, not_1_out);
  not not_3 (not_3_out, clock_1_out);
  not not_4 (not_4_out, not_3_out);
  not not_5 (not_5_out, clock_1_out);
  not not_6 (not_6_out, not_5_out);
  not not_7 (not_7_out, clock_1_out);
  not not_8 (not_8_out, not_7_out);
  not not_9 (not_9_out, clock_1_out);
  not not_10 (not_10_out, clock_1_out);
  not not_11 (not_11_out, clock_1_out);
  not not_12 (not_12_out, clock_1_out);
  not not_13 (not_13_out, not_2_out);
  not not_14 (not_14_out, not_4_out);
  not not_15 (not_15_out, not_6_out);
  not not_16 (not_16_out, not_8_out);
  not not_17 (not_17_out, not_9_out);
  not not_18 (not_18_out, not_17_out);
  not not_19 (not_19_out, not_10_out);
  not not_20 (not_20_out, not_19_out);
  not not_21 (not_21_out, not_11_out);
  not not_22 (not_22_out, not_21_out);
  not not_23 (not_23_out, not_12_out);
  not not_24 (not_24_out, not_23_out);
  and and_1 (and_1_out, clock_1_out, not_13_out);
  and and_2 (and_2_out, clock_1_out, not_14_out);
  and and_3 (and_3_out, clock_1_out, not_15_out);
  and and_4 (and_4_out, clock_1_out, not_16_out);
  and and_5 (and_5_out, clock_1_out, not_18_out);
  and and_6 (and_6_out, clock_1_out, not_20_out);
  and and_7 (and_7_out, clock_1_out, not_22_out);
  and and_8 (and_8_out, clock_1_out, not_24_out);
  and and_9 (and_9_out, and_1_out, Enable);
  and and_10 (and_10_out, and_2_out, Enable);
  and and_11 (and_11_out, and_3_out, Enable);
  and and_12 (and_12_out, and_4_out, Enable);
  and and_13 (and_13_out, and_5_out, Enable);
  not not_25 (not_25_out, D);
  not not_26 (not_26_out, D);
  not not_27 (not_27_out, D);
  not not_28 (not_28_out, D);
  not not_29 (not_29_out, D);
  not not_30 (not_30_out, D);
  and and_14 (and_14_out, and_6_out, Enable);
  not not_31 (not_31_out, D);
  and and_15 (and_15_out, and_7_out, Enable);
  not not_32 (not_32_out, D);
  and and_16 (and_16_out, and_8_out, Enable);
  and and_17 (and_17_out, not_25_out, and_9_out);
  and and_18 (and_18_out, and_9_out, D);
  and and_19 (and_19_out, not_26_out, and_10_out);
  and and_20 (and_20_out, and_10_out, D);
  and and_21 (and_21_out, not_27_out, and_11_out);
  and and_22 (and_22_out, and_11_out, D);
  and and_23 (and_23_out, not_28_out, and_12_out);
  and and_24 (and_24_out, and_12_out, D);
  and and_25 (and_25_out, not_29_out, and_13_out);
  and and_26 (and_26_out, and_13_out, D);
  and and_27 (and_27_out, not_30_out, and_14_out);
  and and_28 (and_28_out, and_14_out, D);
  and and_29 (and_29_out, not_31_out, and_15_out);
  and and_30 (and_30_out, and_15_out, D);
  and and_31 (and_31_out, not_32_out, and_16_out);
  and and_32 (and_32_out, and_16_out, D);
  nor nor_1 (out_3, and_17_out, nor_2_out);
  nor nor_2 (nor_2_out, out_3, and_18_out);
  nor nor_3 (out_4, and_19_out, nor_4_out);
  nor nor_4 (nor_4_out, out_4, and_20_out);
  nor nor_5 (out_5, and_21_out, nor_6_out);
  nor nor_6 (nor_6_out, out_5, and_22_out);
  nor nor_7 (out_6, and_23_out, nor_8_out);
  nor nor_8 (nor_8_out, out_6, and_24_out);
  nor nor_9 (out_7, and_25_out, nor_10_out);
  nor nor_10 (nor_10_out, out_7, and_26_out);
  nor nor_11 (out_8, and_27_out, nor_12_out);
  nor nor_12 (nor_12_out, out_8, and_28_out);
  nor nor_13 (out_9, and_29_out, nor_14_out);
  nor nor_14 (nor_14_out, out_9, and_30_out);
  nor nor_15 (out_10, and_31_out, nor_16_out);
  nor nor_16 (nor_16_out, out_10, and_32_out);
endmodule

module Memory_cell_Dewit (
  input  Enable_pin,
  input  Clock,
  input  Din,
  input  Output_Enable_pin,
  input  Reset,
  output Dout,
  output StoredData
);

  wire and_1_out, and_2_out, not_1_out, or_1_out;

  not not_1 (not_1_out, Enable_pin);
  and and_1 (and_1_out, StoredData, not_1_out);
  and and_2 (and_2_out, Enable_pin, Din);
  or or_1 (or_1_out, and_1_out, and_2_out);
  D_Flip_Flop_part D_FF (.D(or_1_out), .clk(Clock), .Q(StoredData), .reset(Reset));  // open: Qn, preset
  assign Dout = Output_Enable_pin ? StoredData : 1'bz;  // Controlled_Buffer Controlled_Buffer
endmodule

module Register_Dewit (
  input  Output_Enable,
  input  Reset,
  input  Clock,
  input  Enable,
  input  [7:0] Din,
  output [7:0] Dout,
  output [7:0] Stored
);

  Memory_cell_Dewit B0 (
    .Enable_pin(Enable), .Clock(Clock), .Din(Din[0]), .Output_Enable_pin(Output_Enable), .Reset(Reset),
    .Dout(Dout[0]), .StoredData(Stored[0]));
  Memory_cell_Dewit B1 (
    .Enable_pin(Enable), .Clock(Clock), .Din(Din[1]), .Output_Enable_pin(Output_Enable), .Reset(Reset),
    .Dout(Dout[1]), .StoredData(Stored[1]));
  Memory_cell_Dewit B2 (
    .Enable_pin(Enable), .Clock(Clock), .Din(Din[2]), .Output_Enable_pin(Output_Enable), .Reset(Reset),
    .Dout(Dout[2]), .StoredData(Stored[2]));
  Memory_cell_Dewit B3 (
    .Enable_pin(Enable), .Clock(Clock), .Din(Din[3]), .Output_Enable_pin(Output_Enable), .Reset(Reset),
    .Dout(Dout[3]), .StoredData(Stored[3]));
  Memory_cell_Dewit B7 (
    .Enable_pin(Enable), .Clock(Clock), .Din(Din[7]), .Output_Enable_pin(Output_Enable), .Reset(Reset),
    .Dout(Dout[7]), .StoredData(Stored[7]));
  Memory_cell_Dewit B6 (
    .Enable_pin(Enable), .Clock(Clock), .Din(Din[6]), .Output_Enable_pin(Output_Enable), .Reset(Reset),
    .Dout(Dout[6]), .StoredData(Stored[6]));
  Memory_cell_Dewit B5 (
    .Enable_pin(Enable), .Clock(Clock), .Din(Din[5]), .Output_Enable_pin(Output_Enable), .Reset(Reset),
    .Dout(Dout[5]), .StoredData(Stored[5]));
  Memory_cell_Dewit B4 (
    .Enable_pin(Enable), .Clock(Clock), .Din(Din[4]), .Output_Enable_pin(Output_Enable), .Reset(Reset),
    .Dout(Dout[4]), .StoredData(Stored[4]));
endmodule

module MAR (
  input  Clock,
  input  Output_Enable,
  input  Reset,
  input  Enable,
  input  [3:0] in_5,
  output [3:0] Dout,
  output [3:0] Stored
);

  Memory_cell_Dewit memory_cell_dewit_1 (
    .Enable_pin(Enable), .Clock(Clock), .Din(in_5[0]), .Output_Enable_pin(Output_Enable), .Reset(Reset),
    .Dout(Dout[0]), .StoredData(Stored[0]));
  Memory_cell_Dewit memory_cell_dewit_2 (
    .Enable_pin(Enable), .Clock(Clock), .Din(in_5[1]), .Output_Enable_pin(Output_Enable), .Reset(Reset),
    .Dout(Dout[1]), .StoredData(Stored[1]));
  Memory_cell_Dewit memory_cell_dewit_3 (
    .Enable_pin(Enable), .Clock(Clock), .Din(in_5[2]), .Output_Enable_pin(Output_Enable), .Reset(Reset),
    .Dout(Dout[2]), .StoredData(Stored[2]));
  Memory_cell_Dewit memory_cell_dewit_4 (
    .Enable_pin(Enable), .Clock(Clock), .Din(in_5[3]), .Output_Enable_pin(Output_Enable), .Reset(Reset),
    .Dout(Dout[3]), .StoredData(Stored[3]));
endmodule

module ALU_Dewit (
  input  [7:0] RegA,
  input  [7:0] RegB,
  input  OutPut_Enable,
  output [7:0] Dout,
  output [7:0] ALU_Register,
  output Cout
);

  Adder adder_1 (.a(RegA), .b(RegB), .out(ALU_Register), .cout(Cout));  // open: cin
  assign Dout = OutPut_Enable ? ALU_Register : 8'bz;  // Controlled_Buffer controlled_buffer_1
endmodule

module DecimalDecoder (
  input  [7:0] Din,
  output [31:0] Dout
);

  ROM #(.dataWidth(32)) rom_1 (
    .addr(Din),
    .data({Dout[31:28], Dout[15:12], Dout[27:24], Dout[11:8], Dout[23:20], Dout[7:4], Dout[19:16], Dout[3:0]}));

  // Notes on the sheet:
  //   contents of rom_1 (hex, n*v repeats v):
  //   ffffffe7 21 ffffffcb 6b 2d 6e ffffffee 23 ffffffef 2f ffffffe7 21 ffffffcb 6b 2d 6e ffffffee 23
  //   ffffffef 2f ffffffe7 21 ffffffcb 6b 2d 6e ffffffee 23 ffffffef 2f ffffffe7 21 ffffffcb 6b 2d 6e
  //   ffffffee 23 ffffffef 2f ffffffe7 21 ffffffcb 6b 2d 6e ffffffee 23 ffffffef 2f ffffffe7 21 ffffffcb
  //   6b 2d 6e ffffffee 23 ffffffef 2f ffffffe7 21 ffffffcb 6b 2d 6e ffffffee 23 ffffffef 2f ffffffe7 21
  //   ffffffcb 6b 2d 6e ffffffee 23 ffffffef 2f ffffffe7 21 ffffffcb 6b 2d 6e ffffffee 23 ffffffef 2f
  //   ffffffe7 21 ffffffcb 6b 2d 6e ffffffee 23 ffffffef 2f ffffffe7 21 ffffffcb 6b 2d 6e ffffffee 23
  //   ffffffef 2f ffffffe7 21 ffffffcb 6b 2d 6e ffffffee 23 ffffffef 2f ffffffe7 21 ffffffcb 6b 2d 6e
  //   ffffffee 23 ffffffef 2f ffffffe7 21 ffffffcb 6b 2d 6e ffffffee 23 ffffffef 2f ffffffe7 21 ffffffcb
  //   6b 2d 6e ffffffee 23 ffffffef 2f ffffffe7 21 ffffffcb 6b 2d 6e ffffffee 23 ffffffef 2f ffffffe7 21
  //   ffffffcb 6b 2d 6e ffffffee 23 ffffffef 2f ffffffe7 21 ffffffcb 6b 2d 6e ffffffee 23 ffffffef 2f
  //   ffffffe7 21 ffffffcb 6b 2d 6e ffffffee 23 ffffffef 2f ffffffe7 21 ffffffcb 6b 2d 6e ffffffee 23
  //   ffffffef 2f ffffffe7 21 ffffffcb 6b 2d 6e ffffffee 23 ffffffef 2f ffffffe7 21 ffffffcb 6b 2d 6e
  //   ffffffee 23 ffffffef 2f ffffffe7 21 ffffffcb 6b 2d 6e ffffffee 23 ffffffef 2f ffffffe7 21 ffffffcb
  //   6b 2d 6e ffffffee 23 ffffffef 2f ffffffe7 21 ffffffcb 6b 2d 6e ffffffee 23 ffffffef 2f ffffffe7 21
  //   ffffffcb 6b 2d 6e
endmodule

module CUI (
  input  OpC3,
  input  OpC2,
  input  OpC1,
  input  OpC0,
  input  SC2,
  input  SC1,
  input  SC0,
  output C0,
  output C1,
  output C2,
  output C3,
  output C4,
  output C5,
  output C6,
  output C7,
  output C8,
  output C9,
  output C10,
  output C11
);

  wire and_4_out, and_5_out, and_6_out, and_7_out, and_8_out, and_9_out, and_10_out, and_13_out, and_14_out,
       and_15_out, and_16_out, and_17_out, and_18_out, and_19_out, and_20_out, and_21_out, not_1_out,
       not_2_out, not_3_out, not_4_out, not_5_out;

  not not_1 (not_1_out, OpC1);
  not not_2 (not_2_out, OpC0);
  not not_3 (not_3_out, SC2);
  not not_4 (not_4_out, SC1);
  not not_5 (not_5_out, SC0);
  and and_1 (C0, not_3_out, not_4_out, not_5_out);
  and and_2 (C1, not_3_out, not_4_out, SC0);
  and and_3 (C2, OpC1, OpC0, SC2, not_4_out, not_5_out);
  and and_4 (and_4_out, not_3_out, not_4_out, SC0);
  and and_5 (and_5_out, not_1_out, SC2, not_4_out, not_5_out);
  and and_6 (and_6_out, not_3_out, not_4_out, SC0);
  and and_7 (and_7_out, not_1_out, SC2, not_4_out, not_5_out);
  and and_8 (and_8_out, OpC1, OpC0, not_3_out, SC0);
  and and_9 (and_9_out, not_3_out, SC1, not_5_out);
  and and_10 (and_10_out, not_1_out, SC2, not_4_out, SC0);
  and and_11 (C6, OpC1, OpC0, SC2, not_4_out, not_5_out);
  and and_12 (C7, not_3_out, SC1, not_5_out);
  and and_13 (and_13_out, not_1_out, not_2_out, not_3_out, SC1, SC0);
  and and_14 (and_14_out, OpC1, OpC0, not_3_out, SC1, SC0);
  and and_15 (and_15_out, not_3_out, not_4_out, not_5_out);
  and and_16 (and_16_out, not_1_out, not_3_out, SC1, SC0);
  and and_17 (and_17_out, OpC0, not_3_out, SC1, SC0);
  and and_18 (and_18_out, not_3_out, not_4_out, SC0);
  and and_19 (and_19_out, not_1_out, SC2, not_4_out, not_5_out);
  and and_20 (and_20_out, not_1_out, OpC0, not_3_out, SC0);
  and and_21 (and_21_out, OpC0, SC2, not_4_out, not_5_out);
  and and_22 (C11, OpC1, not_2_out, not_3_out, SC1, SC0);
  or or_1 (C3, and_4_out, and_5_out);
  or or_2 (C4, and_6_out, and_7_out, and_8_out);
  or or_3 (C5, and_9_out, and_10_out);
  or or_4 (C8, and_13_out, and_14_out);
  or or_5 (C9, and_15_out, and_16_out, and_17_out);
  or or_6 (C10, and_18_out, and_19_out, and_20_out, and_21_out);
endmodule

module CUII (
  input  OpC3,
  input  OpC2,
  input  OpC1,
  input  OpC0,
  input  SC2,
  input  SC1,
  input  SC0,
  output C12,
  output C13,
  output C14,
  output C15
);

  wire not_1_out, not_2_out, not_3_out, not_4_out;

  not not_1 (not_1_out, OpC1);
  not not_2 (not_2_out, OpC0);
  not not_3 (not_3_out, SC2);
  not not_4 (not_4_out, SC1);
  and and_1 (C12, not_1_out, not_2_out, SC2, not_4_out, SC0);
  and and_2 (C13, not_1_out, OpC0, SC2, not_4_out, SC0);
  and and_3 (C14, OpC1, OpC0, not_3_out, SC1, SC0);
  and and_4 (C15, OpC1, not_2_out, not_3_out, SC1, SC0);
endmodule
